# Fritzing sketch LM35,LED (saved by Fritzing 0.9.4)
breadboards: 1

parts:
  Part1 = Arduino Uno (Rev3)
  LED1 = LED - 5mm [color="Green (560nm)" package="5 mm [THT]"]
  LED2 = LED - 5mm [color="Green (560nm)" package="5 mm [THT]"]
  R1 = Resistor [tolerance=±5% resistance=180 package=THT]
  R2 = Resistor [tolerance=±5% resistance=180 package=THT]
  T1 = LM35 Temperature Sensor [package="TO92 [THT]"]

nets:
  N1: Part1.A1, T1.Vout
  N2: Part1.D8, R1.Pin_1
  N3: Part1.D9_PWM, R2.Pin_1
  GND: Part1.GND, LED1.cathode, LED2.cathode, T1.GND
  N4: Part1.5V, T1.+Vs
  N5: LED1.anode, R2.Pin_0
  N6: LED2.anode, R1.Pin_0
